# Fritzing sketch schema (saved by Fritzing 0.9.9b)
breadboards: 1

parts:
  M1 = BMP280
  Part1 = ESP-WROOM-32 [ESP-32S] Module [part_number=ESP-WROOM-32]

nets:
  VIN: M1.VIN, Part1.3V3
  GND: M1.GND, Part1.GND
  N1: M1.SCL, Part1.CLK
  N2: M1.SDA, Part1.SD1

custom parts:
  BMP280: Temperature Humidity Barometric presure Sensor, I2C
  ESP-WROOM-32 [ESP-32S] Module: Espressif ESP-WROOM-32 WiFi/Bluetooth LE microcontroller module also known as the Ai-Thinker ESP-32S module with similar formfactor. The ESP32 is a microcontroller chip with WiFi and BLE capabilities. The chip is developed by Espressif and is the successor to the popular ESP8266 WiFi module.
